# Fritzing sketch 1-LED-A0-nano (saved by Fritzing 0.9.3b)
breadboards: 1

parts:
  LED1 = LED - 5mm [color="Red (633nm)" package="5 mm [THT]"]
  R1 = Resistor [tolerance=±5% resistance=220 package=THT]
  part = Arduino Nano (Rev3.0)

nets:
  N1: LED1.cathode, R1.Pin_0
  N2: LED1.anode, part.A0
  GND: R1.Pin_1, part.GND
