# Fritzing sketch LED-bateria-resistencias-paralelo (saved by Fritzing 0.8.7b)
circuit board: 1.94504cm x 1.59296cm
breadboards: 1

parts:
  R1 = Resistor [tolerance=±5% resistance=220 package=THT]
  LED1 = LED - 5mm [color="Red (633nm)" package="5 mm [THT]"]
  VCC1 = Battery
  R2 = Resistor [tolerance=±5% resistance=330 package=THT]
  R3 = Resistor [tolerance=±5% resistance=1k package=THT]

nets (from the breadboard view):
  N1: R1.Pin_0, LED1.anode, R2.Pin_1, R3.Pin_1
  N2: R1.Pin_1, VCC1.+, R2.Pin_0, R3.Pin_0
  N3: LED1.cathode, VCC1.-
