# Fritzing sketch arudino_motor_cd (saved by Fritzing 0.9.3b)
breadboards: 1

parts:
  part = Arduino Uno (Rev3)
  part_2 = L293D [package=THT]
  part_3 = DC Motor
  part_4 = Battery block 9V

nets:
  N1: part.D10_PWM/SS, part_2.Enable_1
  N2: part.5V, part_2.In_1, part_2.+V
  GND: part.GND, part_2.0V, part_2.In_2, part_4.-
  N3: part_2.Out_1_(_Controlled_by_Enable_1_), part_3.pin_1
  N4: part_2.Out_2_(_Controlled_by_Enable_1_), part_3.pin_2
  N5: part_2.+Vmotor, part_4.+
