# Fritzing sketch arduino-l293d-stepper (saved by Fritzing 0.9.3b)
breadboards: 1

parts:
  IC1 = L293D [package=THT]
  M1 = Stepper Motor - Bipolar
  VCC1 = Battery block 9V
  Componente1 = Arduino Uno (Rev3)

nets:
  N1: IC1.Enable_1, IC1.Enable_2, IC1.+V, Componente1.5V
  N2: IC1.In_1, Componente1.D10_PWM/SS
  N3: IC1.Out_1_(_Controlled_by_Enable_1_), M1.D
  GND: IC1.0V, VCC1.-, Componente1.GND
  N4: IC1.Out_2_(_Controlled_by_Enable_1_), M1.B
  N5: IC1.In_2, Componente1.D11_PWM/MOSI
  N6: IC1.+Vmotor, VCC1.+
  N7: IC1.In_3, Componente1.D12/MISO
  N8: IC1.Out_3_(_Controlled_by_Enable_2_), M1.C
  N9: IC1.Out_4_(_Controlled_by_Enable_2_), M1.A
  N10: IC1.In_4, Componente1.D13/SCK
